# Fritzing sketch nodemcu_lamb (saved by Fritzing 0.9.3b)
breadboards: 1

parts:
  U1 = NodeMCU V3.0
  Relay_5V1 = Keyes Relay [package=THT]
  LED4 = LEDs [package=led10mm]
  S1 = SPST Switch [package=r_sw_th]

nets:
  N1: U1.D3, Relay_5V1.signal
  N2: U1.VU, Relay_5V1.power
  N3: U1.GND, Relay_5V1.ground
  N4: Relay_5V1.NO, S1.P
  N5: LED4.C, S1.O

notes:
  FAZ
  NOTR

custom parts:
  NodeMCU V3.0: ESP8266 based NodeMCU
  Keyes Relay: The Keyes 5V relay module is suitable for SCM development, home appliance control. It uses a 5V~12V TIL control signal which can control DC / AC signal.
  LEDs: LEDs Standard schematic elements and footprints for 5mm, 3mm, 1206, and 0603 sized LEDs. 5mm - Spark Fun Electronics SKU : COM-00529 (and others)
